// Logisim project new_arc.circ as structural Verilog: 4 circuits, main circuit main
module main (
  input  [7:0] in_1,
  input  in_2,
  input  in_3,
  input  [7:0] in_4,
  input  [7:0] in_5,
  input  [6:0] in_6,
  output [7:0] out_7
);

  wire clock_1_out;

  Clock clock_1 (.out(clock_1_out));
  _8bit_reg u_8bit_reg_1 (.in_1(in_1), .in_2(clock_1_out), .in_3(in_2));  // open: out_6, in_4, out_5
  _8bit_reg u_8bit_reg_2 (.in_1(in_1), .in_2(clock_1_out), .in_3(in_3));  // open: out_6, in_4, out_5
  ALU alu_1 (.in_1(in_4), .in_3(in_5), .out_4(out_7), .in_2(in_6));
endmodule

module _8bit_reg (
  input  [7:0] in_1,
  input  in_2,
  input  in_3,
  input  in_4,
  output [7:0] out_5,
  output [7:0] out_6
);

  wire and_1_out;

  and and_1 (and_1_out, in_2, in_3);
  D_Flip_Flop #(.trigger("falling")) d_ff_1 (
    .clk(and_1_out), .D(in_1[0]), .Q(out_5[0]));  // open: Qn, preset, en, reset
  D_Flip_Flop #(.trigger("falling")) d_ff_2 (
    .clk(and_1_out), .D(in_1[1]), .Q(out_5[1]));  // open: Qn, preset, en, reset
  D_Flip_Flop #(.trigger("falling")) d_ff_3 (
    .clk(and_1_out), .D(in_1[2]), .Q(out_5[2]));  // open: Qn, preset, en, reset
  D_Flip_Flop #(.trigger("falling")) d_ff_4 (
    .clk(and_1_out), .D(in_1[3]), .Q(out_5[3]));  // open: Qn, preset, en, reset
  D_Flip_Flop #(.trigger("falling")) d_ff_5 (
    .clk(and_1_out), .D(in_1[4]), .Q(out_5[4]));  // open: Qn, preset, en, reset
  D_Flip_Flop #(.trigger("falling")) d_ff_6 (
    .clk(and_1_out), .D(in_1[5]), .Q(out_5[5]));  // open: Qn, preset, en, reset
  D_Flip_Flop #(.trigger("falling")) d_ff_7 (
    .clk(and_1_out), .D(in_1[6]), .Q(out_5[6]));  // open: Qn, preset, en, reset
  D_Flip_Flop #(.trigger("falling")) d_ff_8 (
    .clk(and_1_out), .D(in_1[7]), .Q(out_5[7]));  // open: Qn, preset, en, reset
  assign out_6 = in_4 ? out_5 : 8'bz;  // Controlled_Buffer controlled_buffer_1
endmodule

module ALU (
  input  [7:0] in_1,
  input  [6:0] in_2,
  input  [7:0] in_3,
  output [7:0] out_4
);

  wire [7:0] adder_1_out, and_1_out, controled_inv_1_out_3, controled_inv_2_out_3, controled_inv_3_out_3,
       multiplexer_1_out, multiplexer_2_out, multiplexer_3_out;

  controled_inv controled_inv_1 (.in_1(multiplexer_1_out), .in_2(in_2[1]), .out_3(controled_inv_1_out_3));
  Multiplexer #(.width(8), .enable("false")) multiplexer_1 (
    .in0(in_1), .in1({8{1'b0}}), .out(multiplexer_1_out), .sel(in_2[0]));
  Multiplexer #(.width(8), .enable("false")) multiplexer_2 (
    .in0(in_3), .in1({8{1'b0}}), .out(multiplexer_2_out), .sel(in_2[2]));
  controled_inv controled_inv_2 (.in_1(multiplexer_2_out), .in_2(in_2[3]), .out_3(controled_inv_2_out_3));
  Adder adder_1 (.a(controled_inv_1_out_3), .b(controled_inv_2_out_3), .out(adder_1_out));  // open: cin, cout
  assign and_1_out = controled_inv_1_out_3 & controled_inv_2_out_3;  // AND_Gate and_1, 8 bits wide
  Multiplexer #(.width(8), .enable("false")) multiplexer_3 (
    .in0(adder_1_out), .in1(and_1_out), .out(multiplexer_3_out), .sel(in_2[5]));
  controled_inv controled_inv_3 (.in_1(multiplexer_3_out), .in_2(in_2[4]), .out_3(controled_inv_3_out_3));
  assign out_4 = in_2[6] ? controled_inv_3_out_3 : 8'bz;  // Controlled_Buffer controlled_buffer_1

  // Notes on the sheet:
  //   X
  //   Z x
  //   INV X
  //   Y
  //   Z y
  //   INV Y
  //   INV out
  //   X+Y||X&Y
  //   0           1
endmodule

module controled_inv (
  input  [7:0] in_1,
  input  in_2,
  output [7:0] out_3
);

  xor xor_1 (out_3[0], in_1[0], in_2);
  xor xor_2 (out_3[1], in_1[1], in_2);
  xor xor_3 (out_3[2], in_1[2], in_2);
  xor xor_4 (out_3[3], in_1[3], in_2);
  xor xor_5 (out_3[4], in_1[4], in_2);
  xor xor_6 (out_3[5], in_1[5], in_2);
  xor xor_7 (out_3[6], in_1[6], in_2);
  xor xor_8 (out_3[7], in_1[7], in_2);
endmodule
